# Fritzing sketch CircuitSchematic (saved by Fritzing 0.9.3b)

parts:
  U1 = Mini-360 DC-DC Buck converter [package=THT]
  U2 = NodeMCU V3.0
  Part1 = Arduino Uno (Rev3) - ICSP
  Power_plug1 = Power plug
  LED1 = smd LED [color="Red (633nm)" package="1206 [SMD]"]
  Q1 = Basic FET N-Channel [package="D2Pak [SMD]"]
  Part2 = Barometric Pressure Sensor - BMP180 Breakout (GY-68)
  LED2 = smd LED [color="Red (633nm)" package="1206 [SMD]"]
  Q2 = Basic FET N-Channel [package="D2Pak [SMD]"]
  LED3 = smd LED [color="Red (633nm)" package="1206 [SMD]"]
  Q3 = Basic FET N-Channel [package="D2Pak [SMD]"]
  U3 = Mini-360 DC-DC Buck converter [package=THT]
  Part3 = Barometric Pressure Sensor - BMP180 Breakout (GY-68)

nets:
  N1: U1.IN-, Power_plug1.GND, LED1.cathode, LED2.cathode, LED3.cathode, U3.IN-
  N2: U1.IN+, Power_plug1.VCC, Q1.source, Q2.source, Q3.source, U3.IN+
  N3: U1.OUT+, Part1.VIN
  GND: U1.OUT-, Part1.GND, Part2.GND, Part3.GND
  N4: U2.Vin, U3.OUT+
  N5: U2.GND, U3.OUT-
  N6: Part1.A4/SDA, Part2.SDA, Part3.SDA
  N7: Part1.A5/SCL, Part2.SCL, Part3.SCL
  N8: Part1.D5_PWM, Q1.Gate, Q2.Gate, Q3.Gate
  VCC: Part1.3V3, Part2.VCC, Part3.VCC
  N9: LED1.anode, Q1.drain
  N10: LED2.anode, Q2.drain
  N11: LED3.anode, Q3.drain

custom parts:
  Mini-360 DC-DC Buck converter: Mini-360 DC-DC Buck converter. Tiny buck step down voltage converter, input voltage 4.75 to 23V output 1 to 17V adjustable. Available from ebay and the like.
  NodeMCU V3.0: ESP8266 based NodeMCU
