# Fritzing sketch CircuitSchematicNodeMCUOnly (saved by Fritzing 0.9.3b)

parts:
  U2 = NodeMCU V3.0
  12_V_DC = Power plug
  LED1 = smd LED [color="Red (633nm)" package="1206 [SMD]"]
  Q1 = Basic FET N-Channel [package="D2Pak [SMD]"]
  LED2 = smd LED [color="Green (570nm)" package="1206 [SMD]"]
  Q2 = Basic FET N-Channel [package="D2Pak [SMD]"]
  LED3 = smd LED [color="Blue (525nm)" package="1206 [SMD]"]
  Q3 = Basic FET N-Channel [package="D2Pak [SMD]"]
  5V = Mini-360 DC-DC Buck converter [package=THT]
  Fan_1 = Fan - Ventilador [package=THT]
  Q5 = Basic FET N-Channel [package="D2Pak [SMD]"]
  Fan_2 = Fan - Ventilador [package=THT]
  Internal_BMP_280 = Barometric Pressure Sensor - BMP180 Breakout (GY-68)
  External_BMP280 = Barometric Pressure Sensor - BMP180 Breakout (GY-68)
  LED4 = smd LED [color="Blue (525nm)" package="1206 [SMD]"]
  LED5 = smd LED [color="Green (570nm)" package="1206 [SMD]"]
  LED6 = smd LED [color="Red (633nm)" package="1206 [SMD]"]
  Q6 = Basic FET N-Channel [package="D2Pak [SMD]"]
  Q7 = Basic FET N-Channel [package="D2Pak [SMD]"]
  Q8 = Basic FET N-Channel [package="D2Pak [SMD]"]

nets:
  N1: U2.D1, Internal_BMP_280.SCL, External_BMP280.SCL
  N2: U2.D2, Internal_BMP_280.SDA, External_BMP280.SDA
  N3: U2.D3, Q6.Gate
  N4: U2.D4, Q7.Gate
  VCC: U2.3V3, Internal_BMP_280.VCC, External_BMP280.VCC
  GND: U2.GND, 5V.OUT-, Internal_BMP_280.GND, External_BMP280.GND
  N5: U2.D5, Q8.Gate
  N6: U2.D6, Q1.Gate
  N7: U2.D7, Q2.Gate
  N8: U2.D8, Q3.Gate
  N9: U2.RX, Q5.Gate
  N10: U2.Vin, 5V.OUT+
  N11: 12_V_DC.VCC, Q1.source, Q2.source, Q3.source, 5V.IN+, Q5.source, Q6.source, Q7.source, Q8.source
  N12: 12_V_DC.GND, 5V.IN-
  GND_2: LED1.cathode, LED2.cathode, LED3.cathode, Fan_1.GND, Fan_2.GND, LED4.cathode, LED5.cathode, LED6.cathode
  N13: LED1.anode, Q1.drain
  N14: LED2.anode, Q2.drain
  N15: LED3.anode, Q3.drain
  5V: Fan_1.5V, Q5.drain, Fan_2.5V
  N16: LED4.anode, Q6.drain
  N17: LED5.anode, Q7.drain
  N18: LED6.anode, Q8.drain

custom parts:
  NodeMCU V3.0: ESP8266 based NodeMCU
  Mini-360 DC-DC Buck converter: Mini-360 DC-DC Buck converter. Tiny buck step down voltage converter, input voltage 4.75 to 23V output 1 to 17V adjustable. Available from ebay and the like.
  Fan - Ventilador: Ventilador de 2 pines, se encuentra comunmente en computadoras de escritorio
